# Fritzing sketch Esquema de conexão (saved by Fritzing 0.9.3b)
breadboards: 1

parts:
  Componente1 = Arduino Leonardo (Rev3b)
  U1 = MLX90614 [package=to-39]
  hc-sr1 = hc-sr04
  J1 = Basic Servo
  RFID1 = RFID Reader
  LED1 = smd LED [color="Red (633nm)" package="0805 [SMD]"]
  LED2 = smd LED [color="Red (633nm)" package="0805 [SMD]"]
  LED3 = LED - 3mm [color="Red (633nm)" package="3 mm [THT]"]
  LED4 = smd LED [color="Red (633nm)" package="1206 [SMD]"]
  R1 = Resistor [tolerance=±5% resistance=220 package="2512 [SMD]"]
  R2 = Resistor [tolerance=±5% resistance=220 package="1206 [SMD]"]
  R3 = Resistor [tolerance=±5% resistance=220 package="2512 [SMD]"]
  R4 = Resistor [tolerance=±5% resistance=220 package="1206 [SMD]"]

nets:
  N1: Componente1.D1/TX, hc-sr1.Echo
  N2: Componente1.D2/SDA, hc-sr1.Trig
  N3: Componente1.D3_PWM/SCL, J1.pulse
  N4: Componente1.D4/A6, U1.PWM_SDA
  N5: Componente1.D5_PWM, R2.Pin_1
  N6: Componente1.D6_PWM/A7, R1.Pin_1
  N7: Componente1.D7, R4.Pin_0
  3V3: Componente1.3V3, U1.VDD, hc-sr1.VCC
  5V: Componente1.5V, RFID1.+5V
  GND: Componente1.GND, U1.VSS, hc-sr1.GND, RFID1.GND, LED1.cathode, LED2.cathode, LED3.cathode, LED4.cathode
  N8: Componente1.D8/A8, R3.Pin_0
  N9: Componente1.D9_PWM/A9, RFID1.RES
  N10: Componente1.D10_PWM/A10, RFID1.CP
  N11: Componente1.D11_PWM, RFID1.ANT0
  N12: Componente1.D12/A11, RFID1.ANT1
  N13: Componente1.D13_PWM, RFID1.+/-
  N14: LED1.anode, R2.Pin_0
  N15: LED2.anode, R1.Pin_0
  N16: LED3.anode, R3.Pin_1
  N17: LED4.anode, R4.Pin_1
